// Logisim project 16Bit_CPU.circ as structural Verilog: 10 circuits, main circuit Pip_CPU
module RegisterFile (
  input  [2:0] RB,
  input  [2:0] RA,
  input  [2:0] RW,
  input  RegWrite,
  input  [15:0] BusW,
  output [15:0] BusA,
  output [15:0] BusB
);

  wire and_1_out, and_2_out, and_3_out, and_4_out, and_5_out, and_6_out, and_7_out, clock_1_out,
       decoder_1_out1, decoder_1_out2, decoder_1_out3, decoder_1_out4, decoder_1_out5, decoder_1_out6,
       decoder_1_out7, decoder_2_out0, decoder_2_out1, decoder_2_out2, decoder_2_out3, decoder_2_out4,
       decoder_2_out5, decoder_2_out6, decoder_2_out7, decoder_3_out0, decoder_3_out1, decoder_3_out2,
       decoder_3_out3, decoder_3_out4, decoder_3_out5, decoder_3_out6, decoder_3_out7;
  wire [15:0] R1_q, R2_q, R3_q, R4_q, R5_q, R6_q, R7_q;

  Decoder #(.enable("false"), .select(3)) decoder_1 (
    .out1(decoder_1_out1), .out2(decoder_1_out2), .out3(decoder_1_out3), .out4(decoder_1_out4),
    .out5(decoder_1_out5), .out6(decoder_1_out6), .out7(decoder_1_out7), .sel(RW));  // open: out0
  Clock clock_1 (.out(clock_1_out));
  and and_1 (and_1_out, decoder_1_out1, RegWrite);
  and and_2 (and_2_out, decoder_1_out2, RegWrite);
  and and_3 (and_3_out, decoder_1_out3, RegWrite);
  and and_4 (and_4_out, decoder_1_out4, RegWrite);
  and and_5 (and_5_out, decoder_1_out5, RegWrite);
  and and_6 (and_6_out, decoder_1_out6, RegWrite);
  and and_7 (and_7_out, decoder_1_out7, RegWrite);
  Register #(.width(16)) R1 (.D(BusW), .en(and_1_out), .clk(clock_1_out), .Q(R1_q));  // open: clr
  Register #(.width(16)) R2 (.D(BusW), .en(and_2_out), .clk(clock_1_out), .Q(R2_q));  // open: clr
  Register #(.width(16)) R3 (.D(BusW), .en(and_3_out), .clk(clock_1_out), .Q(R3_q));  // open: clr
  Register #(.width(16)) R4 (.D(BusW), .en(and_4_out), .clk(clock_1_out), .Q(R4_q));  // open: clr
  Register #(.width(16)) R5 (.D(BusW), .en(and_5_out), .clk(clock_1_out), .Q(R5_q));  // open: clr
  Register #(.width(16)) R6 (.D(BusW), .en(and_6_out), .clk(clock_1_out), .Q(R6_q));  // open: clr
  Register #(.width(16)) R7 (.D(BusW), .en(and_7_out), .clk(clock_1_out), .Q(R7_q));  // open: clr
  assign BusA = decoder_2_out1 ? R1_q : 16'bz;  // Controlled_Buffer controlled_buffer_1
  assign BusA = decoder_2_out2 ? R2_q : 16'bz;  // Controlled_Buffer controlled_buffer_2
  assign BusA = decoder_2_out3 ? R3_q : 16'bz;  // Controlled_Buffer controlled_buffer_3
  assign BusA = decoder_2_out4 ? R4_q : 16'bz;  // Controlled_Buffer controlled_buffer_4
  assign BusA = decoder_2_out5 ? R5_q : 16'bz;  // Controlled_Buffer controlled_buffer_5
  assign BusA = decoder_2_out6 ? R6_q : 16'bz;  // Controlled_Buffer controlled_buffer_6
  assign BusA = decoder_2_out7 ? R7_q : 16'bz;  // Controlled_Buffer controlled_buffer_7
  Decoder #(.enable("false"), .select(3)) decoder_2 (
    .out0(decoder_2_out0), .out1(decoder_2_out1), .out2(decoder_2_out2), .out3(decoder_2_out3),
    .out4(decoder_2_out4), .out5(decoder_2_out5), .out6(decoder_2_out6), .out7(decoder_2_out7), .sel(RA));
  assign BusA = decoder_2_out0 ? {16{1'b0}} : 16'bz;  // Controlled_Buffer controlled_buffer_8
  assign BusB = decoder_3_out1 ? R1_q : 16'bz;  // Controlled_Buffer controlled_buffer_9
  assign BusB = decoder_3_out2 ? R2_q : 16'bz;  // Controlled_Buffer controlled_buffer_10
  assign BusB = decoder_3_out3 ? R3_q : 16'bz;  // Controlled_Buffer controlled_buffer_11
  assign BusB = decoder_3_out4 ? R4_q : 16'bz;  // Controlled_Buffer controlled_buffer_12
  assign BusB = decoder_3_out5 ? R5_q : 16'bz;  // Controlled_Buffer controlled_buffer_13
  assign BusB = decoder_3_out6 ? R6_q : 16'bz;  // Controlled_Buffer controlled_buffer_14
  assign BusB = decoder_3_out7 ? R7_q : 16'bz;  // Controlled_Buffer controlled_buffer_15
  Decoder #(.enable("false"), .select(3)) decoder_3 (
    .out0(decoder_3_out0), .out1(decoder_3_out1), .out2(decoder_3_out2), .out3(decoder_3_out3),
    .out4(decoder_3_out4), .out5(decoder_3_out5), .out6(decoder_3_out6), .out7(decoder_3_out7), .sel(RB));
  assign BusB = decoder_3_out0 ? {16{1'b0}} : 16'bz;  // Controlled_Buffer controlled_buffer_16
endmodule

module Main_CPU (
  input  PCRst
);

  wire ALUSrc, clock_1_out, clock_2_out, comparator_1_eq, ExtOp, JR, MemRd, MemWr, RegDst, RegWr, WBdata,
       Zero;
  wire [1:0] f, LUI_JAL_slct, PCSrc;
  wire [2:0] multiplexer_2_out, multiplexer_3_out, multiplexer_4_out, spliter_1_rd, spliter_1_rs,
       spliter_1_rt;
  wire [3:0] alucontrol_1_aluop;
  wire [4:0] imm5, OpCode;
  wire [10:0] imm11;
  wire [15:0] adder_2_out, Address, BusW, DataIn, Ext_imm5, Ext_imm11, multiplexer_1_out, multiplexer_5_out,
       multiplexer_6_out, PC, PC_PLUS_1, ram_1_dout, registerfile_1_busa, rom_1_data, shifter_1_out, undriven;

  Clock clock_1 (.out(clock_1_out));
  Register #(.width(16)) register_1 (.D(multiplexer_1_out), .en(1'b1), .Q(PC), .clk(clock_1_out), .clr(PCRst));
  Multiplexer #(.select(2), .width(16)) multiplexer_1 (
    .in0(PC_PLUS_1), .in1(Ext_imm11), .in2(adder_2_out), .in3(registerfile_1_busa), .out(multiplexer_1_out),
    .sel(PCSrc));
  PCsource pcsource_1 (.Op(OpCode), .Zero(Zero), .JR(JR), .PCsrc(PCSrc));
  Adder #(.width(16)) adder_1 (.a(16'h1), .b(PC), .out(PC_PLUS_1));  // open: cin, cout
  ROM #(.addrWidth(16), .dataWidth(16)) rom_1 (.addr(PC), .data(rom_1_data));
  Adder #(.width(16)) adder_2 (.a(PC), .b(Ext_imm5), .out(adder_2_out));  // open: cin, cout
  Spliter spliter_1 (
    .I(rom_1_data), .imm11(imm11), .Rt(spliter_1_rt), .Rs(spliter_1_rs), .Rd(spliter_1_rd), .f(f),
    .OpCode(OpCode), .imm5(imm5));
  Multiplexer #(.width(3)) multiplexer_2 (
    .in0(spliter_1_rt), .in1(spliter_1_rd), .out(multiplexer_2_out), .sel(RegDst));
  Multiplexer #(.width(3)) multiplexer_3 (
    .in0(spliter_1_rt), .in1(multiplexer_4_out), .out(multiplexer_3_out), .sel(comparator_1_eq));
  Multiplexer #(.select(2), .width(3)) multiplexer_4 (
    .in0(multiplexer_2_out), .in1(3'b001), .in2(3'b111), .out(multiplexer_4_out), .sel(LUI_JAL_slct));  // open: in3
  extender extender_1 (.imm11(imm11), .imm5(imm5), .ExtOp(ExtOp), .Ext_imm11(Ext_imm11), .Ext_imm5(Ext_imm5));
  Shifter #(.width(16)) shifter_1 (.in(Ext_imm11), .\dist (4'b0101), .out(shifter_1_out));
  Comparator #(.width(5)) comparator_1 (.a(OpCode), .b(5'b00011), .eq(comparator_1_eq));  // open: gt, lt
  Multiplexer #(.select(2), .width(16)) multiplexer_5 (
    .in0(BusW), .in1(shifter_1_out), .in2(PC_PLUS_1), .in3(undriven), .out(multiplexer_5_out),
    .sel(LUI_JAL_slct));
  main_control main_control_1 (
    .OpCode(OpCode), .ExtOp(ExtOp), .ALUSrc(ALUSrc), .LUI_JAL_slt(LUI_JAL_slct), .MemRd(MemRd),
    .MemWr(MemWr), .WBdata(WBdata), .RegDst(RegDst), .RegWrite(RegWr));
  RegisterFile registerfile_1 (
    .RW(multiplexer_4_out), .RA(spliter_1_rs), .RB(multiplexer_3_out), .RegWrite(RegWr),
    .BusW(multiplexer_5_out), .BusA(registerfile_1_busa), .BusB(DataIn));
  Multiplexer #(.width(16)) multiplexer_6 (.in0(DataIn), .in1(Ext_imm5), .out(multiplexer_6_out), .sel(ALUSrc));
  ALU alu_1 (
    .Input1(registerfile_1_busa), .Input2(multiplexer_6_out), .ALUOp(alucontrol_1_aluop), .Output1(Address),
    .ZERO(Zero), .JR(JR));
  ALUcontrol alucontrol_1 (.Op(OpCode), .fun(f), .ALUOp(alucontrol_1_aluop));
  Clock clock_2 (.out(clock_2_out));
  RAM #(.addrWidth(16), .dataWidth(16)) ram_1 (
    .addr(Address), .we(MemWr), .oe(MemRd), .clk(clock_2_out), .din(DataIn), .dout(ram_1_dout));
  Multiplexer #(.width(16)) multiplexer_7 (.in0(Address), .in1(ram_1_dout), .out(BusW), .sel(WBdata));

  // Other names for the same wires on the sheet: ALUResult[15:0] = Address

  // Notes on the sheet:
  //   Make PCsrc is 1 when Op is JAl (10001)
  //   Make PCSrc is 3 when is JR
  //   contents of rom_1 (hex, n*v repeats v):
  //   4141 a88 51c3 d1a 95c f84 495f 4a 28b 4f2 732 5955 104a 12f2 1532 175a ff6c 1c88 1a50 1888 4182 6914
  //   6115 6895 168 cc9 7918 47db 70eb 4001 7959 77a5 0 0 0 8030 7009 11*0 4283 4004 40c5 6815 4064 4052
  //   7f63 4001 883a 8024 0 c92 4243 4006 680e 4049 4076 680e 67cc 600d 1ac 4049 4052 7e93 1e38
endmodule

module Instruction_Memory (
);

  wire PC_Ctrl;
  wire [1:0] f;
  wire [2:0] imm5;
  wire [4:0] Op;
  wire [5:0] imm11;
  wire [15:0] multiplexer_1_out, PC, PC_PLUS_2;

  Multiplexer #(.width(16)) multiplexer_1 (.in0(PC_PLUS_2), .out(multiplexer_1_out), .sel(PC_Ctrl));  // open: in1
  Adder #(.width(16)) adder_1 (.a(16'h2), .b(PC), .out(PC_PLUS_2));  // open: cin, cout
  Register #(.width(16)) InstrectionRegister_PC (.D(multiplexer_1_out), .Q(PC));  // open: en, clk, clr
  ROM #(.addrWidth(16), .dataWidth(16)) rom_1 (.addr(PC), .data({Op, f, imm5, imm11}));
  // RegisterFile registerfile_1: pin names not known; wires that end beside it: imm11[5:3], imm5

  // Other names for the same wires on the sheet: Rt[2:0] = imm11[2:0]; Rs[2:0] = imm11[5:3]; imm11[10:6] = {f, imm5};
  //   Rd[2:0] = imm5; imm5[4:3] = f
endmodule

module Spliter (
  input  [15:0] I,
  output [4:0] OpCode,
  output [10:0] imm11,
  output [2:0] Rt,
  output [2:0] Rs,
  output [2:0] Rd,
  output [1:0] f,
  output [4:0] imm5
);


  assign f = I[10:9];
  assign imm5 = I[10:6];
  assign imm11 = I[10:0];
  assign OpCode = I[15:11];
  assign Rd = I[8:6];
  assign Rs = I[5:3];
  assign Rt = I[2:0];
endmodule

module main_control (
  input  [4:0] OpCode,
  output RegDst,
  output ExtOp,
  output RegWrite,
  output MemRd,
  output ALUSrc,
  output MemWr,
  output WBdata,
  output [1:0] LUI_JAL_slt
);

  wire ADD_SUB_SLT_SLTU, ADDI, AND_OR_XOR_NOR, ANDI, BEQ, BNE, J, ORI, REVL_REVH_REVA_JR, SLL_SRL_SRA_ROR,
       XORI;

  Decoder #(.enable("false"), .select(5)) decoder_1 (
    .out0(ADD_SUB_SLT_SLTU), .out1(AND_OR_XOR_NOR), .out2(SLL_SRL_SRA_ROR), .out3(REVL_REVH_REVA_JR),
    .out8(ADDI), .out9(ANDI), .out10(ORI), .out11(XORI), .out12(MemRd), .out13(MemWr), .out14(BEQ),
    .out15(BNE), .out16(J), .out17(LUI_JAL_slt[1]), .out31(LUI_JAL_slt[0]), .sel(OpCode));  // open: out4, out5, out6, out7, out18, out19, out20, out21, out22, out23, out24, out25, out26, out27, out28, out29, out30
  nor nor_1 (ExtOp, J, ANDI, XORI, ORI, LUI_JAL_slt[1]);
  nor nor_2 (ALUSrc, RegDst, BNE, BEQ);
  or or_1 (RegDst, ADD_SUB_SLT_SLTU, AND_OR_XOR_NOR, SLL_SRL_SRA_ROR, REVL_REVH_REVA_JR);
  nor nor_3 (RegWrite, MemWr, BEQ, BNE, J);

  assign WBdata = MemRd;

  // Other names for the same wires on the sheet: LUI = LUI_JAL_slt[0]; JAL = LUI_JAL_slt[1]; LW = MemRd;
  //   R_TYPE = RegDst; SW = MemWr
endmodule

module PCsource (
  input  [4:0] Op,
  input  Zero,
  input  JR,
  output [1:0] PCsrc
);

  wire and_1_out, and_2_out, and_3_out, and_4_out, and_5_out, not_1_out, not_2_out, not_3_out, not_4_out,
       not_5_out, not_6_out;

  not not_1 (not_1_out, Op[4]);
  not not_2 (not_2_out, Op[3]);
  not not_3 (not_3_out, Op[2]);
  not not_4 (not_4_out, Op[1]);
  not not_5 (not_5_out, Op[0]);
  not not_6 (not_6_out, Zero);
  and and_1 (and_1_out, not_1_out, Op[3], Op[2], Op[1], not_5_out, Zero);
  and and_2 (and_2_out, not_1_out, Op[3], Op[2], Op[1], Op[0], not_6_out);
  and and_3 (and_3_out, not_1_out, not_2_out, not_3_out, Op[1], Op[0], JR);
  and and_4 (and_4_out, Op[4], not_2_out, not_3_out, not_4_out);
  and and_5 (and_5_out, not_1_out, not_2_out, not_3_out, Op[1], Op[0], JR);
  or or_1 (PCsrc[1], and_1_out, and_2_out, and_3_out);
  or or_2 (PCsrc[0], and_4_out, and_5_out);
endmodule

module Pip_CPU (
  output [1:0] out_1
);

  wire ALUSrc, clock_1_out, clock_2_out, clock_3_out, clock_4_out, clock_5_out, clock_6_out, clock_7_out,
       clock_8_out, comparator_1_eq, comparator_2_eq, ExMemRd, ExRegWr, ExtOp, JR, kill2,
       main_ctrl_pip_1_alusrc, main_ctrl_pip_1_memrd, main_ctrl_pip_1_memwr, main_ctrl_pip_1_regwrite,
       main_ctrl_pip_1_wbdata, MemRd, MEMRegWr, MemWr, not_1_out, not_2_out, or_1_out, pcsourcepip_1_kill1,
       RegDst, register_3_q, register_4_q, register_13_q, RegWr, Stall, WBdata, Zero;
  wire [1:0] f, ForwardA, ForwardB, LUI_JAL_slct;
  wire [2:0] multiplexer_3_out, multiplexer_5_out, Rd2, Rd3, Rd4, Rs, Rt, spliter_1_rd, spliter_1_rt;
  wire [3:0] alucontrol_1_aluop, ALUOp_q;
  wire [4:0] imm5, multiplexer_4_out, OpCode;
  wire [10:0] imm11;
  wire [15:0] A_q, adder_2_out, alu_1_output1, bit_extender_1_out, BusW, D_q, DataIn, Ext_imm5, Ext_imm11,
       extender_1_ext_imm5, extender_1_ext_imm11, Inst_q, multiplexer_1_out, multiplexer_2_out,
       multiplexer_7_out, multiplexer_8_out, multiplexer_9_out, multiplexer_10_out, multiplexer_11_out,
       multiplexer_12_out, NPC_q, PC_PLUS_1, PC_q, R_q, ram_1_dout, register_1_q, register_2_q,
       registerfile_1_busa, registerfile_1_busb, rom_1_data, shifter_1_out, undriven;

  not not_1 (not_1_out, Stall);
  Clock clock_1 (.out(clock_1_out));
  Register #(.width(16)) PC (.D(multiplexer_1_out), .en(not_1_out), .Q(PC_q), .clk(clock_1_out));  // open: clr
  ROM #(.addrWidth(16), .dataWidth(16)) rom_1 (.addr(PC_q), .data(rom_1_data));
  Multiplexer #(.select(2), .width(16)) multiplexer_1 (
    .in0(PC_PLUS_1), .in1(bit_extender_1_out), .in2(adder_2_out), .in3(registerfile_1_busa),
    .out(multiplexer_1_out), .sel(out_1));
  Adder #(.width(16)) adder_1 (.a(16'h1), .b(PC_q), .out(PC_PLUS_1));  // open: cin, cout
  PCsourcepip pcsourcepip_1 (
    .Op(OpCode), .Zero(Zero), .JR(JR), .PCsrc(out_1), .kill1(pcsourcepip_1_kill1), .kill2(kill2));
  Register #(.width(16)) NPC (.D(PC_PLUS_1), .en(1'b1), .Q(NPC_q), .clk(clock_2_out));  // open: clr
  Clock clock_2 (.out(clock_2_out));
  Adder #(.width(16)) adder_2 (.a(NPC_q), .b(Ext_imm5), .out(adder_2_out));  // open: cin, cout
  Multiplexer #(.width(16)) multiplexer_2 (
    .in0(rom_1_data), .in1({16{1'b0}}), .out(multiplexer_2_out), .sel(pcsourcepip_1_kill1));
  assign bit_extender_1_out = {{5{1'b0}}, imm11};  // Bit_Extender bit_extender_1
  Register #(.width(16)) Inst (.D(multiplexer_2_out), .en(not_2_out), .Q(Inst_q), .clk(clock_3_out));  // open: clr
  Clock clock_3 (.out(clock_3_out));
  not not_2 (not_2_out, Stall);
  Spliter spliter_1 (
    .I(Inst_q), .imm11(imm11), .Rt(spliter_1_rt), .Rs(Rs), .Rd(spliter_1_rd), .f(f), .OpCode(OpCode),
    .imm5(imm5));
  ForwardControl forwardcontrol_1 (
    .Rs(Rs), .Rd2(Rd2), .ExRegWr(ExRegWr), .Rd3(Rd3), .MEMRegWr(MEMRegWr), .Rd4(Rd4), .WBRegWr(RegWr),
    .MemR(ExMemRd), .Rt(Rt), .ForwardA(ForwardA), .stall(Stall), .ForwardB(ForwardB));
  Multiplexer #(.select(2), .width(3)) multiplexer_3 (
    .in0(spliter_1_rd), .in1(3'b001), .in2(3'b111), .out(multiplexer_3_out), .sel(LUI_JAL_slct));  // open: in3
  Multiplexer #(.width(5)) multiplexer_4 (.in0(OpCode), .in1({5{1'b0}}), .out(multiplexer_4_out), .sel(or_1_out));
  or or_1 (or_1_out, Stall, kill2);
  Multiplexer #(.width(3)) multiplexer_5 (
    .in0(spliter_1_rt), .in1(multiplexer_3_out), .out(multiplexer_5_out), .sel(RegDst));
  Clock clock_4 (.out(clock_4_out));
  Register #(.width(16)) register_1 (.D(PC_PLUS_1), .en(1'b1), .Q(register_1_q), .clk(clock_4_out));  // open: clr
  Multiplexer #(.width(3)) multiplexer_6 (.in0(spliter_1_rt), .in1(spliter_1_rd), .out(Rt), .sel(comparator_1_eq));
  Register #(.width(16)) register_2 (.D(register_1_q), .en(1'b1), .Q(register_2_q), .clk(clock_4_out));  // open: clr
  extender extender_1 (
    .imm11(imm11), .imm5(imm5), .ExtOp(ExtOp), .Ext_imm11(extender_1_ext_imm11),
    .Ext_imm5(extender_1_ext_imm5));
  Clock clock_5 (.out(clock_5_out));
  Register #(.width(16)) BTA (.D(extender_1_ext_imm11), .en(1'b1), .Q(Ext_imm11), .clk(clock_5_out));  // open: clr
  Register #(.width(16)) Imm (.D(extender_1_ext_imm5), .en(1'b1), .Q(Ext_imm5), .clk(clock_5_out));  // open: clr
  Comparator #(.width(5)) comparator_1 (.a(OpCode), .b(5'b00011), .eq(comparator_1_eq));  // open: gt, lt
  Multiplexer #(.select(2), .width(16)) multiplexer_7 (
    .in0(BusW), .in1(BusW), .in2(register_2_q), .in3(undriven), .out(multiplexer_7_out), .sel(LUI_JAL_slct));
  Clock clock_6 (.out(clock_6_out));
  main_ctrl_pip main_ctrl_pip_1 (
    .OpCode(multiplexer_4_out), .RegDst(RegDst), .ExtOp(ExtOp), .ALUSrc(main_ctrl_pip_1_alusrc),
    .MemRd(main_ctrl_pip_1_memrd), .RegWrite(main_ctrl_pip_1_regwrite), .MemWr(main_ctrl_pip_1_memwr),
    .WBdata(main_ctrl_pip_1_wbdata), .LUI_JAL_slt(LUI_JAL_slct));
  RegisterFile registerfile_1 (
    .RW(Rd4), .RA(Rs), .RB(Rt), .RegWrite(RegWr), .BusW(multiplexer_7_out), .BusA(registerfile_1_busa),
    .BusB(registerfile_1_busb));
  Register #(.width(1)) register_3 (
    .D(main_ctrl_pip_1_wbdata), .en(1'b1), .Q(register_3_q), .clk(clock_6_out));  // open: clr
  Register #(.width(1)) register_4 (
    .D(main_ctrl_pip_1_memwr), .en(1'b1), .Q(register_4_q), .clk(clock_6_out));  // open: clr
  Register #(.width(1)) register_5 (.D(main_ctrl_pip_1_memrd), .en(1'b1), .Q(ExMemRd), .clk(clock_6_out));  // open: clr
  Register #(.width(1)) register_6 (.D(main_ctrl_pip_1_alusrc), .en(1'b1), .Q(ALUSrc), .clk(clock_6_out));  // open: clr
  Register #(.width(1)) register_7 (
    .D(main_ctrl_pip_1_regwrite), .en(1'b1), .Q(ExRegWr), .clk(clock_6_out));  // open: clr
  Register #(.width(1)) register_8 (.D(register_3_q), .en(1'b1), .Q(WBdata), .clk(clock_6_out));  // open: clr
  Register #(.width(1)) register_9 (.D(register_4_q), .en(1'b1), .Q(MemWr), .clk(clock_6_out));  // open: clr
  Register #(.width(1)) register_10 (.D(ExMemRd), .en(1'b1), .Q(MemRd), .clk(clock_6_out));  // open: clr
  Register #(.width(1)) register_11 (.D(ExRegWr), .en(1'b1), .Q(MEMRegWr), .clk(clock_6_out));  // open: clr
  Register #(.width(1)) register_12 (.D(MEMRegWr), .en(1'b1), .Q(RegWr), .clk(clock_6_out));  // open: clr
  Multiplexer #(.select(2), .width(16)) multiplexer_8 (
    .in0(registerfile_1_busa), .in1(multiplexer_11_out), .in2(multiplexer_12_out), .in3(multiplexer_7_out),
    .out(multiplexer_8_out), .sel(ForwardA));
  Multiplexer #(.select(2), .width(16)) multiplexer_9 (
    .in0(registerfile_1_busb), .in1(multiplexer_11_out), .in2(multiplexer_12_out), .in3(multiplexer_7_out),
    .out(multiplexer_9_out), .sel(ForwardB));
  Clock clock_7 (.out(clock_7_out));
  Register #(.width(16)) A (.D(multiplexer_8_out), .en(1'b1), .Q(A_q), .clk(clock_7_out));  // open: clr
  Register #(.width(16)) B (.D(multiplexer_9_out), .en(1'b1), .Q(DataIn), .clk(clock_7_out));  // open: clr
  Register #(.width(3)) u_RD2 (.D(multiplexer_5_out), .en(1'b1), .Q(Rd2), .clk(clock_6_out));  // open: clr
  Multiplexer #(.width(16)) multiplexer_10 (.in0(DataIn), .in1(Ext_imm5), .out(multiplexer_10_out), .sel(ALUSrc));
  ALUcontrol alucontrol_1 (.Op(OpCode), .fun(f), .ALUOp(alucontrol_1_aluop));
  ALU alu_1 (.Input1(A_q), .Input2(multiplexer_10_out), .ALUOp(ALUOp_q), .Output1(alu_1_output1), .ZERO(Zero), .JR(JR));
  Register #(.width(4)) ALUOp (.D(alucontrol_1_aluop), .en(1'b1), .Q(ALUOp_q), .clk(clock_6_out));  // open: clr
  Shifter #(.width(16)) shifter_1 (.in(Ext_imm11), .\dist (4'b0101), .out(shifter_1_out));
  Comparator #(.width(2)) comparator_2 (.a(LUI_JAL_slct), .b(2'b01), .eq(comparator_2_eq));  // open: gt, lt
  Multiplexer #(.width(16)) multiplexer_11 (
    .in0(alu_1_output1), .in1(shifter_1_out), .out(multiplexer_11_out), .sel(register_13_q));
  Register #(.width(1)) register_13 (
    .D(comparator_2_eq), .en(1'b1), .Q(register_13_q), .clk(clock_8_out));  // open: clr
  Clock clock_8 (.out(clock_8_out));
  Register #(.width(16)) R (.D(multiplexer_11_out), .en(1'b1), .Q(R_q), .clk(clock_8_out));  // open: clr
  Register #(.width(16)) D (.D(DataIn), .en(1'b1), .Q(D_q), .clk(clock_8_out));  // open: clr
  Register #(.width(3)) u_RD3 (.D(Rd2), .en(1'b1), .Q(Rd3), .clk(clock_6_out));  // open: clr
  RAM #(.addrWidth(16), .dataWidth(16), .trigger("falling")) ram_1 (
    .addr(R_q), .we(MemWr), .oe(MemRd), .clk(clock_8_out), .din(D_q), .dout(ram_1_dout));
  Multiplexer #(.width(16)) multiplexer_12 (.in0(R_q), .in1(ram_1_dout), .out(multiplexer_12_out), .sel(WBdata));
  Register #(.width(3)) u_RD4 (.D(Rd3), .en(1'b1), .Q(Rd4), .clk(clock_6_out));  // open: clr
  Register #(.width(16)) Dataa (.D(multiplexer_12_out), .en(1'b1), .clk(clock_8_out), .Q(BusW));  // open: clr

  // Other names for the same wires on the sheet: PCSrc[1:0] = out_1; WBRegWr = RegWr

  // Notes on the sheet:
  //   contents of rom_1 (hex, n*v repeats v):
  //   4141 a88 51c3 d1a 95c f84 495f 4a 28b 4f2 732 5955 104a 12f2 1532 175a ff6c 1c88 1a50 1888 4182 6914
  //   6115 68d5 168 cc9 7918 47db 70eb 4001 7959 77a5 0 0 0 8030 7009 11*0 4283 4004 40c5 6815 4064 4052
  //   7f63 4001 883a 8024 0 c92 4243 4006 680e 4049 4076 680e 67cc 600d 1ac 4049 4052 7e93 1e38
  //   Make PCSrc is 3 when is JR
  //   Make PCsrc is 1 when Op is JAl (10001)
  //   this ram is falling edge 
endmodule

module extender (
  input  [10:0] imm11,
  input  [4:0] imm5,
  input  ExtOp,
  output [15:0] Ext_imm11,
  output [15:0] Ext_imm5
);

  wire [15:0] bit_extender_2_out, bit_extender_3_out;

  assign Ext_imm11 = {{5{1'b0}}, imm11};  // Bit_Extender bit_extender_1
  assign bit_extender_2_out = {{11{1'b0}}, imm5};  // Bit_Extender bit_extender_2
  assign bit_extender_3_out = {{11{imm5[4]}}, imm5};  // Bit_Extender bit_extender_3
  Multiplexer #(.width(16)) multiplexer_1 (
    .in0(bit_extender_2_out), .in1(bit_extender_3_out), .out(Ext_imm5), .sel(ExtOp));
endmodule

module main_ctrl_pip (
  input  [4:0] OpCode,
  output RegDst,
  output ExtOp,
  output ALUSrc,
  output MemRd,
  output RegWrite,
  output MemWr,
  output WBdata,
  output [1:0] LUI_JAL_slt
);

  wire ADD_SUB_SLT_SLTU, ADDI, AND_OR_XOR_NOR, ANDI, BEQ, BNE, clock_1_out, clock_2_out, decoder_1_out14,
       decoder_1_out15, J, NoOp, nor_1_out, nor_2_out, nor_3_out, not_1_out, not_2_out, not_3_out, ORI,
       REVL_REVH_REVA_JR, SLL_SRL_SRA_ROR, XORI;

  Decoder #(.enable("false"), .select(5)) decoder_1 (
    .out0(ADD_SUB_SLT_SLTU), .out1(AND_OR_XOR_NOR), .out2(SLL_SRL_SRA_ROR), .out3(REVL_REVH_REVA_JR),
    .out8(ADDI), .out9(ANDI), .out10(ORI), .out11(XORI), .out12(MemRd), .out13(MemWr),
    .out14(decoder_1_out14), .out15(decoder_1_out15), .out16(J), .out17(LUI_JAL_slt[1]), .out30(NoOp),
    .out31(LUI_JAL_slt[0]), .sel(OpCode));  // open: out4, out5, out6, out7, out18, out19, out20, out21, out22, out23, out24, out25, out26, out27, out28, out29
  Clock clock_1 (.out(clock_1_out));
  Clock clock_2 (.out(clock_2_out));
  Register #(.width(1)) register_1 (.D(decoder_1_out14), .Q(BEQ), .clk(clock_1_out));  // open: en, clr
  Register #(.width(1)) register_2 (.D(decoder_1_out15), .Q(BNE), .clk(clock_2_out));  // open: en, clr
  nor nor_1 (nor_1_out, MemWr, BEQ, BNE, J);
  not not_1 (not_1_out, NoOp);
  and and_1 (RegWrite, not_1_out, nor_1_out);
  not not_2 (not_2_out, NoOp);
  nor nor_2 (nor_2_out, RegDst, BNE, BEQ);
  and and_2 (ALUSrc, not_2_out, nor_2_out);
  or or_1 (RegDst, ADD_SUB_SLT_SLTU, AND_OR_XOR_NOR, SLL_SRL_SRA_ROR, REVL_REVH_REVA_JR, LUI_JAL_slt[0]);
  not not_3 (not_3_out, NoOp);
  nor nor_3 (nor_3_out, J, ANDI, XORI, ORI, LUI_JAL_slt[1]);
  and and_3 (ExtOp, not_3_out, nor_3_out);

  assign WBdata = MemRd;

  // Other names for the same wires on the sheet: LUI = LUI_JAL_slt[0]; JAL = LUI_JAL_slt[1]; LW = MemRd;
  //   R_TYPE = RegDst; SW = MemWr
endmodule

module ForWard (
  input  Reg1,
  input  Reg2,
  input  Reg3,
  input  [2:0] Rs1,
  input  [2:0] Rs2,
  input  [2:0] Rd2,
  input  Rd3,
  input  Rd4
);

  wire and_1_out, comparator_1_eq, comparator_2_eq, Rs1_not_zero;

  Comparator #(.width(3)) comparator_1 (.a(Rs1), .eq(comparator_1_eq));  // open: b, gt, lt
  not not_1 (Rs1_not_zero, comparator_1_eq);
  Comparator #(.width(3)) comparator_2 (.a(Rs1), .b(Rd2), .eq(comparator_2_eq));  // open: gt, lt
  and and_1 (and_1_out, Rs1_not_zero, comparator_2_eq, Reg1);
endmodule
