// Logisim project ALU (1).circ as structural Verilog: 1 circuit, main circuit ALU
module ALU (
  input  [15:0] Input1,
  input  [15:0] Input2,
  input  [3:0] ALUOp,
  output [15:0] Output1,
  output ZERO,
  output JR
);

  wire comparator_1_lt, comparator_2_lt;
  wire [15:0] adder_1_out, and_1_out, bit_extender_1_out, bit_extender_2_out, multiplexer_1_out,
       multiplexer_2_out, multiplexer_3_out, multiplexer_4_out, not_1_out, or_1_out, reva_1_o, revh_1_o,
       revlower_1_o, shifter_1_out, shifter_2_out, shifter_3_out, shifter_4_out, subtractor_1_out, xor_1_out;

  Comparator #(.width(16)) comparator_1 (.a(Input1), .b(Input2), .lt(comparator_1_lt));  // open: gt, eq
  Comparator #(.mode("unsigned"), .width(16)) comparator_2 (
    .a(Input1), .b(Input2), .lt(comparator_2_lt));  // open: gt, eq
  assign and_1_out = Input1 & Input2;  // AND_Gate and_1, 16 bits wide
  assign or_1_out = Input1 | Input2;  // OR_Gate or_1, 16 bits wide
  assign xor_1_out = Input1 ^ Input2;  // XOR_Gate xor_1, 16 bits wide
  Adder #(.width(16)) adder_1 (.a(Input1), .b(Input2), .out(adder_1_out));  // open: cin, cout
  Subtractor #(.width(16)) subtractor_1 (.a(Input1), .b(Input2), .out(subtractor_1_out));  // open: bin, bout
  assign bit_extender_1_out = {{15{1'b0}}, comparator_1_lt};  // Bit_Extender bit_extender_1
  assign bit_extender_2_out = {{15{1'b0}}, comparator_2_lt};  // Bit_Extender bit_extender_2
  assign not_1_out = ~or_1_out;  // NOT_Gate not_1, 16 bits wide
  Shifter #(.width(16)) shifter_1 (.in(Input1), .\dist (Input2[3:0]), .out(shifter_1_out));
  Shifter #(.shift("lr"), .width(16)) shifter_2 (.in(Input1), .\dist (Input2[3:0]), .out(shifter_2_out));
  Shifter #(.shift("ar"), .width(16)) shifter_3 (.in(Input1), .\dist (Input2[3:0]), .out(shifter_3_out));
  Shifter #(.shift("rr"), .width(16)) shifter_4 (.in(Input1), .\dist (Input2[3:0]), .out(shifter_4_out));
  REVLower revlower_1 (.I(Input1), .Dist(Input2), .O(revlower_1_o));
  REVH revh_1 (.\dist (Input2), .I(Input1), .O(revh_1_o));
  REVA reva_1 (.I(Input1), .O(reva_1_o));
  Multiplexer #(.enable("true"), .select(2), .width(16)) multiplexer_1 (
    .in0(adder_1_out), .in1(subtractor_1_out), .in2(bit_extender_1_out), .in3(bit_extender_2_out),
    .out(multiplexer_1_out), .sel(ALUOp[1:0]));  // open: en
  Multiplexer #(.enable("true"), .select(2), .width(16)) multiplexer_2 (
    .in0(and_1_out), .in1(or_1_out), .in2(xor_1_out), .in3(not_1_out), .out(multiplexer_2_out),
    .sel(ALUOp[1:0]));  // open: en
  Multiplexer #(.enable("true"), .select(2), .width(16)) multiplexer_3 (
    .in0(shifter_1_out), .in1(shifter_2_out), .in2(shifter_3_out), .in3(shifter_4_out),
    .out(multiplexer_3_out), .sel(ALUOp[1:0]));  // open: en
  Multiplexer #(.enable("true"), .select(2), .width(16)) multiplexer_4 (
    .in0(revlower_1_o), .in1(revh_1_o), .in2(reva_1_o), .out(multiplexer_4_out), .sel(ALUOp[1:0]));  // open: in3, en
  Multiplexer #(.enable("true"), .select(2), .width(16)) multiplexer_5 (
    .in0(multiplexer_1_out), .in1(multiplexer_2_out), .in2(multiplexer_3_out), .in3(multiplexer_4_out),
    .out(Output1), .sel(ALUOp[3:2]));  // open: en
  Comparator #(.width(16)) comparator_3 (.a(Output1), .b({16{1'b0}}), .eq(ZERO));  // open: gt, lt
  Comparator #(.width(4)) comparator_4 (.a(ALUOp), .b(4'b1111), .eq(JR));  // open: gt, lt

  // Notes on the sheet:
  //   SLT
  //   ADD
  //   SUB
  //   SLTU
  //   AND
  //   OR
  //   XOR
  //   SLL
  //   SRL
  //   SLA
  //   ROR
  //   REVL
  //   NOR
endmodule
