// Logisim project ALU.circ as structural Verilog: 1 circuit, main circuit ALU_circit
module ALU_circit (
  input  [15:0] input1,
  input  [15:0] input2,
  input  [2:0] Operation,
  input  [1:0] functions,
  output [15:0] ZERO,
  output [15:0] output1
);

  wire comparator_1_lt, comparator_2_lt;
  wire [15:0] adder_1_out, and_1_out, bit_extender_1_out, bit_extender_2_out, multiplexer_1_out,
       multiplexer_2_out, multiplexer_4_out, multiplexer_5_out, not_1_out, or_1_out, reva_1_o, revh_1_p2,
       revlower_1_p2, shifter_1_out, shifter_2_out, shifter_3_out, shifter_4_out, subtractor_1_out, xor_1_out;

  assign ZERO = ~(output1 | {16{1'b1}});  // NOR_Gate nor_1, 16 bits wide
  Comparator #(.width(16)) comparator_1 (.a(input1), .b(input2), .lt(comparator_1_lt));  // open: gt, eq
  Comparator #(.mode("unsigned"), .width(16)) comparator_2 (
    .a(input1), .b(input2), .lt(comparator_2_lt));  // open: gt, eq
  assign and_1_out = input1 & input2;  // AND_Gate and_1, 16 bits wide
  assign or_1_out = input1 | input2;  // OR_Gate or_1, 16 bits wide
  assign xor_1_out = input1 ^ input2;  // XOR_Gate xor_1, 16 bits wide
  Adder #(.width(16)) adder_1 (.a(input1), .b(input2), .out(adder_1_out));  // open: cin, cout
  Subtractor #(.width(16)) subtractor_1 (.a(input1), .b(input2), .out(subtractor_1_out));  // open: bin, bout
  assign bit_extender_1_out = {{15{comparator_1_lt}}, comparator_1_lt};  // Bit_Extender bit_extender_1
  assign bit_extender_2_out = {{15{comparator_2_lt}}, comparator_2_lt};  // Bit_Extender bit_extender_2
  assign not_1_out = ~or_1_out;  // NOT_Gate not_1, 16 bits wide
  Shifter #(.width(16)) shifter_1 (.in(input1), .\dist (input2[3:0]), .out(shifter_1_out));
  Shifter #(.shift("lr"), .width(16)) shifter_2 (.in(input1), .\dist (input2[3:0]), .out(shifter_2_out));
  Shifter #(.shift("ar"), .width(16)) shifter_3 (.in(input1), .\dist (input2[3:0]), .out(shifter_3_out));
  Shifter #(.shift("rr"), .width(16)) shifter_4 (.in(input1), .\dist (input2[3:0]), .out(shifter_4_out));
  // REVLower revlower_1: pin names not known; wires that end beside it: input1, revlower_1_p2
  // REVH revh_1: pin names not known; wires that end beside it: input1, revh_1_p2
  REVA reva_1 (.I(input1), .O(reva_1_o));
  Multiplexer #(.enable("true"), .select(2), .width(16)) multiplexer_1 (
    .in0(adder_1_out), .in1(subtractor_1_out), .in2(bit_extender_1_out), .in3(bit_extender_2_out),
    .out(multiplexer_1_out), .sel(functions));  // open: en
  Multiplexer #(.enable("true"), .select(2), .width(16)) multiplexer_2 (
    .in0(and_1_out), .in1(or_1_out), .in2(xor_1_out), .in3(not_1_out), .out(multiplexer_2_out),
    .sel(functions));  // open: en
  Multiplexer #(.enable("true"), .select(3), .width(16)) multiplexer_3 (
    .in0(multiplexer_1_out), .in1(multiplexer_2_out), .in2(multiplexer_4_out), .in3(multiplexer_5_out),
    .out(output1), .sel(Operation));  // open: in4, in5, in6, in7, en
  Multiplexer #(.enable("true"), .select(2), .width(16)) multiplexer_4 (
    .in0(shifter_1_out), .in1(shifter_2_out), .in2(shifter_3_out), .in3(shifter_4_out),
    .out(multiplexer_4_out), .sel(functions));  // open: en
  Multiplexer #(.enable("true"), .select(2), .width(16)) multiplexer_5 (
    .in0(revlower_1_p2), .in1(revh_1_p2), .in2(reva_1_o), .in3(input1), .out(multiplexer_5_out));  // open: sel, en

  // Notes on the sheet:
  //   ADD
  //   SUB
  //   SLT
  //   SLTU
  //   AND
  //   OR
  //   XOR
  //   SLL
  //   SRL
  //   SLA
  //   ROR
  //   REVL
  //   NOR
  //   JR
endmodule
