// Logisim project ALUOp.circ as structural Verilog: 1 circuit, main circuit ALUcontrol
module ALUcontrol (
  input  [4:0] Op,
  input  [1:0] fun,
  output [3:0] ALUOp
);

  wire and_2_out, and_3_out, and_4_out, and_5_out, and_6_out, and_7_out, and_8_out, not_1_out, not_2_out,
       not_3_out;

  not not_1 (not_1_out, Op[3]);
  not not_2 (not_2_out, Op[2]);
  not not_3 (not_3_out, Op[0]);
  and and_1 (ALUOp[3], not_1_out, Op[1]);
  and and_2 (and_2_out, not_2_out, Op[0]);
  and and_3 (and_3_out, Op[3], not_2_out, Op[1]);
  and and_4 (and_4_out, not_1_out, fun[1]);
  and and_5 (and_5_out, Op[3], not_2_out, Op[1], Op[0]);
  and and_6 (and_6_out, not_1_out, fun[0]);
  and and_7 (and_7_out, Op[3], Op[1], not_3_out);
  and and_8 (and_8_out, Op[2], Op[1]);
  or or_1 (ALUOp[2], and_2_out, and_3_out);
  or or_2 (ALUOp[1], and_4_out, and_5_out);
  or or_3 (ALUOp[0], Op[4], and_6_out, and_7_out, and_8_out);
endmodule
