// Logisim project ALU_add_sub_Shfter.circ as structural Verilog: 1 circuit, main circuit main
module main (
  input  [15:0] in_1,
  input  [15:0] in_2,
  input  in_3,
  input  in_4,
  input  [1:0] in_5,
  output [15:0] out_6
);

  wire [15:0] a0_1_p4, shift_1_o;

  // a0 a0_1: pin names not known; wires that end beside it: in_1, in_2, in_3, a0_1_p4
  shift shift_1 (.I(in_1), .in_2(in_2[3:0]), .S(in_5), .O(shift_1_o));
  Multiplexer #(.width(16)) multiplexer_1 (.in0(a0_1_p4), .in1(shift_1_o), .out(out_6), .sel(in_4));
endmodule
