// Logisim project ALUpluse.circ as structural Verilog: 1 circuit, main circuit ALUplus
module ALUplus (
);

  wire [15:0] BusA, BusB, lmmOut, multiplexer_1_out, PC_PLUS1, shifter_1_out;

  Shifter #(.width(16)) shifter_1 (.in(lmmOut), .\dist (4'b0101), .out(shifter_1_out));
  Multiplexer #(.select(2), .width(16)) multiplexer_1 (
    .in0(BusB), .in1(shifter_1_out), .in2(PC_PLUS1), .out(multiplexer_1_out));  // open: in3, sel
  // ALU alu_1: pin names not known; wires that end beside it: BusA, multiplexer_1_out
endmodule
