// Logisim project DataMemory.circ as structural Verilog: 1 circuit, main circuit DataMemeory
module DataMemeory (
  input  [15:0] Address,
  input  EnableWriting,
  input  EnableLoad,
  input  [15:0] Data,
  output [15:0] O
);

  wire clock_1_out;

  Clock clock_1 (.out(clock_1_out));
  RAM #(.addrWidth(16), .dataWidth(16)) ram_1 (
    .addr(Address), .we(EnableWriting), .oe(EnableLoad), .clk(clock_1_out), .din(Data), .dout(O));
endmodule
