// Logisim project ForwardControl_exp.circ as structural Verilog: 2 circuits, main circuit main
module main (
  input  [2:0] Rs,
  input  [2:0] Rd2,
  input  ExRegWr,
  input  [2:0] Rd3,
  input  MEMRegWr,
  input  [2:0] Rd4,
  input  WBRegWr,
  input  MemR,
  input  [2:0] Rt,
  output [1:0] ForwardA,
  output stall,
  output [1:0] ForwardB
);

  wire and_1_out, and_2_out, and_3_out, and_4_out, and_5_out, and_6_out, comparator_1_eq, comparator_2_eq,
       comparator_3_eq, comparator_4_eq, comparator_5_eq, comparator_6_eq, comparator_7_eq, comparator_8_eq,
       nor_1_out, nor_2_out, not_1_out, not_2_out, or_1_out;
  wire [1:0] priority_encoder_1_out, priority_encoder_2_out;

  Comparator #(.width(3)) comparator_1 (.a(Rs), .b(Rd2), .eq(comparator_1_eq));  // open: gt, lt
  Comparator #(.width(3)) comparator_2 (.a(Rs), .b(Rd3), .eq(comparator_2_eq));  // open: gt, lt
  Comparator #(.width(3)) comparator_3 (.a(Rs), .b(Rd4), .eq(comparator_3_eq));  // open: gt, lt
  Comparator #(.width(3)) comparator_4 (.a(Rt), .b(Rd2), .eq(comparator_4_eq));  // open: gt, lt
  Comparator #(.width(3)) comparator_5 (.a(Rt), .b(Rd3), .eq(comparator_5_eq));  // open: gt, lt
  Comparator #(.width(3)) comparator_6 (.a(Rt), .b(Rd4), .eq(comparator_6_eq));  // open: gt, lt
  not not_1 (not_1_out, comparator_7_eq);
  Comparator #(.width(3)) comparator_7 (.a(Rs), .b(3'b000), .eq(comparator_7_eq));  // open: gt, lt
  not not_2 (not_2_out, comparator_8_eq);
  Comparator #(.width(3)) comparator_8 (.a(Rt), .b(3'b000), .eq(comparator_8_eq));  // open: gt, lt
  and and_1 (and_1_out, not_1_out, comparator_1_eq, ExRegWr);
  and and_2 (and_2_out, not_1_out, comparator_2_eq, MEMRegWr);
  and and_3 (and_3_out, not_1_out, comparator_3_eq, WBRegWr);
  and and_4 (and_4_out, not_2_out, ExRegWr, comparator_4_eq);
  and and_5 (and_5_out, not_2_out, MEMRegWr, comparator_5_eq);
  and and_6 (and_6_out, not_2_out, WBRegWr, comparator_6_eq);
  Multiplexer multiplexer_1 ();  // open: in0, in1, out, sel
  Priority_Encoder #(.select(2)) priority_encoder_1 (
    .in0(and_3_out), .in1(and_2_out), .in2(and_1_out), .in3(nor_1_out), .out(priority_encoder_1_out));  // open: gs, en_out, en_in
  nor nor_1 (nor_1_out, and_2_out, and_3_out, and_2_out);
  Priority_Encoder #(.select(2)) priority_encoder_2 (
    .in0(and_6_out), .in1(and_5_out), .in2(and_4_out), .in3(nor_2_out), .out(priority_encoder_2_out));  // open: gs, en_out, en_in
  nor nor_2 (nor_2_out, and_5_out, and_6_out, and_5_out);
  assign ForwardA = ~priority_encoder_1_out;  // NOT_Gate not_3, 2 bits wide
  assign ForwardB = ~priority_encoder_2_out;  // NOT_Gate not_4, 2 bits wide
  or or_1 (or_1_out, and_1_out, and_4_out);
  and and_7 (stall, MemR, or_1_out);
endmodule

module forward_wxp (
  input  [2:0] Rs,
  input  [2:0] Rd2,
  input  ExRegWr,
  input  [2:0] Rd3,
  input  MEMRegWr,
  input  [2:0] Rd4,
  input  WBRegWr,
  input  MemR,
  input  [2:0] Rt,
  output [1:0] ForwardA,
  output stall,
  output [1:0] ForwardB
);

  wire and_1_out, and_2_out, and_3_out, and_4_out, and_5_out, and_6_out, comparator_1_eq, comparator_2_eq,
       comparator_3_eq, comparator_4_eq, comparator_5_eq, comparator_6_eq, comparator_7_eq, comparator_8_eq,
       nor_1_out, nor_2_out, not_1_out, not_2_out, or_1_out;
  wire [1:0] priority_encoder_2_out;

  BitSelector bitselector_1 ();  // open: in, out, sel
  Comparator #(.width(3)) comparator_1 (.a(Rs), .b(Rd2), .eq(comparator_1_eq));  // open: gt, lt
  Comparator #(.width(3)) comparator_2 (.a(Rs), .b(Rd3), .eq(comparator_2_eq));  // open: gt, lt
  Comparator #(.width(3)) comparator_3 (.a(Rs), .b(Rd4), .eq(comparator_3_eq));  // open: gt, lt
  Comparator #(.width(3)) comparator_4 (.a(Rt), .b(Rd2), .eq(comparator_4_eq));  // open: gt, lt
  Comparator #(.width(3)) comparator_5 (.a(Rt), .b(Rd3), .eq(comparator_5_eq));  // open: gt, lt
  Comparator #(.width(3)) comparator_6 (.a(Rt), .b(Rd4), .eq(comparator_6_eq));  // open: gt, lt
  not not_1 (not_1_out, comparator_7_eq);
  Comparator #(.width(3)) comparator_7 (.a(Rs), .b(3'b000), .eq(comparator_7_eq));  // open: gt, lt
  not not_2 (not_2_out, comparator_8_eq);
  Comparator #(.width(3)) comparator_8 (.a(Rt), .b(3'b000), .eq(comparator_8_eq));  // open: gt, lt
  and and_1 (and_1_out, not_1_out, comparator_1_eq, ExRegWr);
  and and_2 (and_2_out, not_1_out, comparator_2_eq, MEMRegWr);
  and and_3 (and_3_out, not_1_out, comparator_3_eq, WBRegWr);
  and and_4 (and_4_out, not_2_out, ExRegWr, comparator_4_eq);
  and and_5 (and_5_out, not_2_out, MEMRegWr, comparator_5_eq);
  and and_6 (and_6_out, not_2_out, WBRegWr, comparator_6_eq);
  Priority_Encoder #(.select(2)) priority_encoder_1 (
    .in0(nor_1_out), .in1(and_1_out), .in2(and_2_out), .in3(and_3_out), .out(ForwardA));  // open: gs, en_out, en_in
  nor nor_1 (nor_1_out, and_2_out, and_3_out, and_2_out);
  Priority_Encoder #(.select(2)) priority_encoder_2 (
    .in0(and_6_out), .in1(and_5_out), .in2(and_4_out), .in3(nor_2_out), .out(priority_encoder_2_out));  // open: gs, en_out, en_in
  nor nor_2 (nor_2_out, and_5_out, and_6_out, and_5_out);
  assign ForwardB = ~priority_encoder_2_out;  // NOT_Gate not_3, 2 bits wide
  or or_1 (or_1_out, and_1_out, and_4_out);
  and and_7 (stall, MemR, or_1_out);
endmodule
