// Logisim project IstSpliter.circ as structural Verilog: 1 circuit, main circuit InstSpliter
module InstSpliter (
  input  [15:0] I,
  output [4:0] OpCode,
  output [10:0] imm11,
  output [4:0] imm5,
  output [2:0] Rs,
  output [2:0] Rt,
  output [2:0] Rd,
  output [1:0] f
);


  assign f = I[10:9];
  assign imm5 = I[10:6];
  assign imm11 = I[10:0];
  assign OpCode = I[15:11];
  assign Rd = I[8:6];
  assign Rs = I[5:3];
  assign Rt = I[2:0];
endmodule
