// Logisim project Logic_Unit.circ as structural Verilog: 1 circuit, main circuit logic
module \logic  (
  input  [15:0] A,
  input  [1:0] C,
  input  [15:0] B,
  output [15:0] OTP
);

  wire [15:0] and_1_out, not_1_out, or_1_out, xor_1_out;

  assign and_1_out = A & B;  // AND_Gate and_1, 16 bits wide
  assign or_1_out = A | B;  // OR_Gate or_1, 16 bits wide
  assign xor_1_out = A ^ B;  // XOR_Gate xor_1, 16 bits wide
  assign not_1_out = ~or_1_out;  // NOT_Gate not_1, 16 bits wide
  Multiplexer #(.enable("true"), .select(2), .width(16)) multiplexer_1 (
    .in0(and_1_out), .in1(or_1_out), .in2(not_1_out), .in3(xor_1_out), .out(OTP), .sel(C));  // open: en
endmodule
