// Logisim project NextPc0.circ as structural Verilog: 1 circuit, main circuit NextPc
module NextPc (
  input  Rst,
  output [15:0] out_2
);

  wire clock_1_out;
  wire [15:0] adder_1_out;

  Clock clock_1 (.out(clock_1_out));
  Register #(.width(16)) register_1 (.D(adder_1_out), .en(1'b1), .Q(out_2), .clk(clock_1_out), .clr(Rst));
  Adder #(.width(16)) adder_1 (.a(16'h1), .b(out_2), .out(adder_1_out));  // open: cin, cout
endmodule
