// Logisim project PCPro.circ as structural Verilog: 1 circuit, main circuit PCPro
module PCPro (
  input  [15:0] D,
  input  PCRst,
  output [15:0] Q
);

  wire clock_1_out;

  Clock clock_1 (.out(clock_1_out));
  Register #(.width(16)) register_1 (.D(D), .en(1'b1), .Q(Q), .clk(clock_1_out), .clr(PCRst));
endmodule
