// Logisim project PCSource.circ as structural Verilog: 1 circuit, main circuit PCsource
module PCsource (
  input  [4:0] Op,
  input  Zero,
  output [1:0] PCsrc
);

  wire not_1_out, not_2_out, not_3_out, not_4_out, not_5_out;

  not not_1 (not_1_out, Op[4]);
  not not_2 (not_2_out, Op[3]);
  not not_3 (not_3_out, Op[2]);
  not not_4 (not_4_out, Op[1]);
  not not_5 (not_5_out, Op[0]);
  and and_1 (PCsrc[1], not_1_out, Op[3], Op[2], Op[1], Zero);
  and and_2 (PCsrc[0], Op[4], not_2_out, not_3_out, not_4_out, not_5_out);
endmodule
