// Logisim project PC_V0.circ as structural Verilog: 2 circuits, main circuit main
module main (
);

  wire [15:0] undriven;

  ROM #(.addrWidth(16), .dataWidth(16)) rom_1 (.addr(undriven));  // open: data
endmodule

module PC (
  input  Rst,
  output [15:0] out_2
);

  wire clock_1_out;
  wire [15:0] adder_1_out;

  Clock clock_1 (.out(clock_1_out));
  Register #(.width(16)) register_1 (.D(adder_1_out), .en(1'b1), .Q(out_2), .clk(clock_1_out), .clr(Rst));
  Adder #(.width(16)) adder_1 (.a(16'h1), .b(out_2), .out(adder_1_out));  // open: cin, cout
endmodule
