// Logisim project REVA.circ as structural Verilog: 1 circuit, main circuit REVA
module REVA (
  input  [15:0] I,
  output [15:0] O
);


  assign O = {I[0], I[1], I[2], I[3], I[4], I[5], I[6], I[7], I[8], I[9], I[10], I[11], I[12], I[13], I[14], I[15]};
endmodule
