// Logisim project REVH.circ as structural Verilog: 1 circuit, main circuit REVH
module REVH (
  input  [15:0] \dist ,
  input  [15:0] I,
  output [15:0] O
);


  assign O = {\dist [15:8], I[8], I[9], I[10], I[11], I[12], I[13], I[14], I[15]};
endmodule
