// Logisim project REVLower.circ as structural Verilog: 1 circuit, main circuit REVLower
module REVLower (
  input  [15:0] I,
  input  [15:0] Dist,
  output [15:0] O
);


  assign O = {Dist[15:8], I[0], I[1], I[2], I[3], I[4], I[5], I[6], I[7]};
endmodule
