// Logisim project adder_suber.circ as structural Verilog: 1 circuit, main circuit a0
module a0 (
  input  [15:0] A,
  input  [15:0] B,
  input  S,
  output [15:0] O
);

  wire [15:0] adder_1_out, subtractor_1_out;

  Adder #(.width(16)) adder_1 (.a(A), .b(B), .out(adder_1_out));  // open: cin, cout
  Subtractor #(.width(16)) subtractor_1 (.a(A), .b(B), .out(subtractor_1_out));  // open: bin, bout
  Multiplexer #(.width(16)) multiplexer_1 (.in0(adder_1_out), .in1(subtractor_1_out), .out(O), .sel(S));
endmodule
