// Logisim project instractionMemo_DataMemo.circ as structural Verilog: 1 circuit, main circuit main
module main (
  input  in_1,
  output [15:0] out_2
);

  wire clock_1_out, CtrlRE, CtrlWE;
  wire [15:0] Adress, DataIn, DataOut, nextpc_1_out_2;

  Clock clock_1 (.out(clock_1_out));
  ROM #(.addrWidth(16), .dataWidth(16)) rom_1 (.addr(nextpc_1_out_2), .data(out_2));
  NextPc nextpc_1 (.Rst(in_1), .out_2(nextpc_1_out_2));
  RAM #(.addrWidth(16), .dataWidth(16)) ram_1 (
    .addr(Adress), .we(CtrlWE), .oe(CtrlRE), .clk(clock_1_out), .din(DataIn), .dout(DataOut));

  // Notes on the sheet:
  //   contents of rom_1 (hex, n*v repeats v):
  //   ad12
endmodule
