// Logisim project shifterr.circ as structural Verilog: 1 circuit, main circuit shift
module shift (
  input  [15:0] I,
  input  [3:0] in_2,
  input  [1:0] S,
  output [15:0] O
);

  wire [15:0] shifter_1_out, shifter_2_out, shifter_3_out, shifter_4_out;

  Shifter #(.width(16)) shifter_1 (.in(I), .\dist (in_2), .out(shifter_1_out));
  Shifter #(.shift("ar"), .width(16)) shifter_2 (.in(I), .\dist (in_2), .out(shifter_2_out));
  Shifter #(.shift("rl"), .width(16)) shifter_3 (.in(I), .\dist (in_2), .out(shifter_3_out));
  Shifter #(.width(16)) shifter_4 (.in(I), .\dist (in_2), .out(shifter_4_out));
  Multiplexer #(.select(2), .width(16)) multiplexer_1 (
    .in0(shifter_1_out), .in1(shifter_2_out), .in2(shifter_3_out), .in3(shifter_4_out), .out(O), .sel(S));
endmodule
