// Logisim project ‏‏PCSourcePip.circ as structural Verilog: 1 circuit, main circuit PCSourcePip
module PCSourcePip (
  input  [4:0] Op,
  input  Zero,
  output [1:0] PCsrc,
  output kill1,
  output kill2
);

  wire and_1_out, and_2_out, and_4_out, and_5_out, and_6_out, and_7_out, and_8_out, not_1_out, not_2_out,
       not_3_out, not_4_out, not_5_out, not_6_out;

  not not_1 (not_1_out, Op[4]);
  not not_2 (not_2_out, Op[3]);
  not not_3 (not_3_out, Op[2]);
  not not_4 (not_4_out, Op[1]);
  not not_5 (not_5_out, Op[0]);
  not not_6 (not_6_out, Zero);
  and and_1 (and_1_out, not_1_out, Op[3], Op[2], Op[1], not_5_out, Zero);
  or or_1 (PCsrc[1], and_1_out, and_2_out);
  and and_2 (and_2_out, not_1_out, Op[3], Op[2], Op[1], Op[0], not_6_out);
  and and_3 (PCsrc[0], Op[4], not_2_out, not_3_out, not_4_out, not_5_out);
  and and_4 (and_4_out, Op[4], not_2_out, not_3_out, not_4_out, not_5_out);
  and and_5 (and_5_out, not_1_out, Op[3], Op[2], Op[1], not_5_out, Zero);
  or or_2 (kill1, and_4_out, and_5_out, and_6_out);
  and and_6 (and_6_out, not_1_out, Op[3], Op[2], Op[1], Op[0], not_6_out);
  and and_7 (and_7_out, not_1_out, Op[3], Op[2], Op[1], not_5_out, Zero);
  or or_3 (kill2, and_7_out, and_8_out);
  and and_8 (and_8_out, not_1_out, Op[3], Op[2], Op[1], Op[0], not_6_out);
endmodule
